// Logisim project ALU assignment1.circ as structural Verilog: 5 circuits, main circuit full adder
// F.A.
module full_adder (
  input  A,
  input  B,
  input  Cin,
  output S,
  output Cout
);

  wire and_1_out, and_2_out, and_3_out, xor_1_out;

  xor xor_1 (xor_1_out, A, B);
  and and_1 (and_1_out, A, B);
  and and_2 (and_2_out, B, Cin);
  and and_3 (and_3_out, A, Cin);
  xor xor_2 (S, xor_1_out, Cin);
  or or_1 (Cout, and_1_out, and_2_out, and_3_out);
endmodule

module _3_bit_multiplier (
  input  B2,
  input  B1,
  input  B0,
  input  A2,
  input  A1,
  input  A0,
  output O5,
  output O4,
  output O3,
  output O2,
  output O1,
  output O0
);

  wire and_2_out, and_3_out, and_4_out, and_5_out, and_6_out, and_7_out, and_8_out, and_9_out,
       full_adder_1_cout, full_adder_2_cout, full_adder_2_s, full_adder_3_cout, full_adder_4_cout,
       full_adder_6_cout, full_adder_6_s;

  and and_1 (O0, B0, A0);
  and and_2 (and_2_out, B0, A1);
  and and_3 (and_3_out, B1, A0);
  and and_4 (and_4_out, B0, A2);
  and and_5 (and_5_out, B1, A1);
  and and_6 (and_6_out, B2, A0);
  and and_7 (and_7_out, B1, A2);
  and and_8 (and_8_out, B2, A1);
  and and_9 (and_9_out, B2, A2);
  full_adder full_adder_1 (.A(and_2_out), .B(and_3_out), .Cin(1'b0), .S(O1), .Cout(full_adder_1_cout));
  full_adder full_adder_2 (
    .A(and_4_out), .B(and_5_out), .Cin(full_adder_1_cout), .S(full_adder_2_s), .Cout(full_adder_2_cout));
  full_adder full_adder_3 (.A(full_adder_2_s), .B(and_6_out), .Cin(1'b0), .S(O2), .Cout(full_adder_3_cout));
  full_adder full_adder_4 (.A(and_7_out), .B(and_8_out), .Cin(full_adder_6_s), .S(O3), .Cout(full_adder_4_cout));
  full_adder full_adder_5 (.A(full_adder_6_cout), .B(and_9_out), .Cin(full_adder_4_cout), .S(O4), .Cout(O5));
  full_adder full_adder_6 (
    .A(full_adder_2_cout), .B(full_adder_3_cout), .Cin(1'b0), .S(full_adder_6_s), .Cout(full_adder_6_cout));
endmodule

module _3_bit_adder (
  input  B2,
  input  B1,
  input  B0,
  input  A2,
  input  A1,
  input  A0,
  output S3,
  output S2,
  output S1,
  output S0
);

  wire full_adder_1_cout, full_adder_2_cout;

  full_adder full_adder_1 (.A(B0), .B(A0), .Cin(1'b0), .S(S0), .Cout(full_adder_1_cout));
  full_adder full_adder_2 (.A(B1), .B(A1), .Cin(full_adder_1_cout), .S(S1), .Cout(full_adder_2_cout));
  full_adder full_adder_3 (.A(B2), .B(A2), .Cin(full_adder_2_cout), .S(S2), .Cout(S3));
endmodule

module alu (
  input  Select,
  input  B1,
  input  B2,
  input  B0,
  input  A2,
  input  Enable,
  input  A1,
  input  A0,
  output O5,
  output O4,
  output O3,
  output O2,
  output O1,
  output O0
);

  wire n3_bit_adder_1_s0, n3_bit_adder_1_s1, n3_bit_adder_1_s2, n3_bit_adder_1_s3, n3_bit_multiplier_1_o0,
       n3_bit_multiplier_1_o1, n3_bit_multiplier_1_o2, n3_bit_multiplier_1_o3, n3_bit_multiplier_1_o4,
       n3_bit_multiplier_1_o5;

  _3_bit_adder u_3_bit_adder_1 (
    .A2(A2), .A1(A1), .A0(A0), .B2(B2), .B1(B1), .B0(B0), .S3(n3_bit_adder_1_s3), .S2(n3_bit_adder_1_s2),
    .S1(n3_bit_adder_1_s1), .S0(n3_bit_adder_1_s0));
  _3_bit_multiplier u_3_bit_multiplier_1 (
    .A2(A2), .A1(A1), .A0(A0), .B2(B2), .B1(B1), .B0(B0), .O5(n3_bit_multiplier_1_o5),
    .O4(n3_bit_multiplier_1_o4), .O3(n3_bit_multiplier_1_o3), .O2(n3_bit_multiplier_1_o2),
    .O1(n3_bit_multiplier_1_o1), .O0(n3_bit_multiplier_1_o0));
  Multiplexer multiplexer_1 (.in0(1'b0), .in1(n3_bit_multiplier_1_o5), .out(O5), .sel(Select), .en(Enable));
  Multiplexer multiplexer_2 (.in0(1'b0), .in1(n3_bit_multiplier_1_o4), .out(O4), .sel(Select), .en(Enable));
  Multiplexer multiplexer_3 (
    .in0(n3_bit_adder_1_s3), .in1(n3_bit_multiplier_1_o3), .out(O3), .sel(Select), .en(Enable));
  Multiplexer multiplexer_4 (
    .in0(n3_bit_adder_1_s2), .in1(n3_bit_multiplier_1_o2), .out(O2), .sel(Select), .en(Enable));
  Multiplexer multiplexer_5 (
    .in0(n3_bit_adder_1_s1), .in1(n3_bit_multiplier_1_o1), .out(O1), .sel(Select), .en(Enable));
  Multiplexer multiplexer_6 (
    .in0(n3_bit_adder_1_s0), .in1(n3_bit_multiplier_1_o0), .out(O0), .sel(Select), .en(Enable));
endmodule

module final_alu (
  input  B1,
  input  B2,
  input  B0,
  input  A2,
  input  A1,
  input  A0,
  input  Enable,
  input  Select,
  output O5,
  output O4,
  output O3,
  output O2,
  output O1,
  output O0
);

  alu alu_1 (
    .A2(A2), .A1(A1), .A0(A0), .B2(B2), .B1(B1), .B0(B0), .Select(Select), .Enable(Enable), .O5(O5), .O4(O4),
    .O3(O3), .O2(O2), .O1(O1), .O0(O0));
endmodule
