// Logisim project Bus assignment1.circ as structural Verilog: 1 circuit, main circuit main
module main (
  input  in_1,
  input  in_2,
  input  in_3,
  input  in_4,
  input  in_5,
  input  in_6,
  input  in_7,
  input  in_8,
  input  in_9,
  input  in_10,
  input  in_11,
  input  in_12,
  input  in_13,
  input  in_14,
  output out_15,
  output out_16,
  output out_17,
  output out_18,
  output out_19,
  output out_20,
  output B0,
  output B1,
  output B2,
  output B3,
  output B4,
  output B5
);

  wire Clk_out, Y0_q, Y1_q, Y2_q, Y3_q, Y4_q, Y5_q;

  Clock Clk (.out(Clk_out));
  D_Flip_Flop X5 (.clk(Clk_out), .D(B5), .Q(out_15), .en(in_1));  // open: Qn, preset, reset
  D_Flip_Flop Y5 (.clk(Clk_out), .D(in_2), .Q(Y5_q), .en(in_8));  // open: Qn, preset, reset
  and and_1 (B5, Y5_q, in_14);
  D_Flip_Flop X4 (.clk(Clk_out), .D(B4), .Q(out_16), .en(in_1));  // open: Qn, preset, reset
  D_Flip_Flop Y4 (.clk(Clk_out), .D(in_3), .Q(Y4_q), .en(in_9));  // open: Qn, preset, reset
  D_Flip_Flop X3 (.clk(Clk_out), .D(B3), .Q(out_17), .en(in_1));  // open: Qn, preset, reset
  D_Flip_Flop Y3 (.clk(Clk_out), .D(in_4), .Q(Y3_q), .en(in_10));  // open: Qn, preset, reset
  and and_2 (B4, Y4_q, in_14);
  D_Flip_Flop X2 (.clk(Clk_out), .D(B2), .Q(out_18), .en(in_1));  // open: Qn, preset, reset
  D_Flip_Flop Y2 (.clk(Clk_out), .D(in_5), .Q(Y2_q), .en(in_11));  // open: Qn, preset, reset
  and and_3 (B3, Y3_q, in_14);
  and and_4 (B2, Y2_q, in_14);
  D_Flip_Flop X1 (.clk(Clk_out), .D(B1), .Q(out_19), .en(in_1));  // open: Qn, preset, reset
  D_Flip_Flop Y1 (.clk(Clk_out), .D(in_6), .Q(Y1_q), .en(in_12));  // open: Qn, preset, reset
  D_Flip_Flop X0 (.clk(Clk_out), .D(B0), .Q(out_20), .en(in_1));  // open: Qn, preset, reset
  D_Flip_Flop Y0 (.clk(Clk_out), .D(in_7), .Q(Y0_q), .en(in_13));  // open: Qn, preset, reset
  and and_5 (B1, Y1_q, in_14);
  and and_6 (B0, Y0_q, in_14);
endmodule
