// Logisim project RAM mudit.circ as structural Verilog: 1 circuit, main circuit main
module main (
  input  _1,
  input  in_2,
  input  in_3,
  input  [1:0] in_4,
  input  in_5,
  output out_6,
  output out_7,
  output out_8,
  output out_9,
  output out_10,
  output out_11
);

  wire clock_1_out, d_ff_1_q, d_ff_2_q, d_ff_3_q, d_ff_4_q, d_ff_5_q, d_ff_6_q, decoder_1_out0,
       decoder_1_out1, decoder_1_out2;

  Decoder #(.select(2)) decoder_1 (
    .out0(decoder_1_out0), .out1(decoder_1_out1), .out2(decoder_1_out2), .sel(in_4), .en(in_3));  // open: out3
  Clock clock_1 (.out(clock_1_out));
  D_Flip_Flop d_ff_1 (.clk(clock_1_out), .D(_1), .Q(d_ff_1_q), .en(decoder_1_out0));  // open: Qn, preset, reset
  D_Flip_Flop d_ff_2 (.clk(clock_1_out), .D(_1), .Q(d_ff_2_q), .en(decoder_1_out1));  // open: Qn, preset, reset
  D_Flip_Flop d_ff_3 (.clk(clock_1_out), .D(_1), .Q(d_ff_3_q), .en(decoder_1_out2));  // open: Qn, preset, reset
  and and_1 (out_8, decoder_1_out0, in_5, d_ff_1_q);
  and and_2 (out_10, d_ff_2_q, in_5, decoder_1_out1);
  and and_3 (out_11, d_ff_3_q, in_5, decoder_1_out2);
  D_Flip_Flop d_ff_4 (.clk(clock_1_out), .D(in_2), .Q(d_ff_4_q), .en(decoder_1_out0));  // open: Qn, preset, reset
  D_Flip_Flop d_ff_5 (.clk(clock_1_out), .D(in_2), .Q(d_ff_5_q), .en(decoder_1_out1));  // open: Qn, preset, reset
  D_Flip_Flop d_ff_6 (.clk(clock_1_out), .D(in_2), .Q(d_ff_6_q), .en(decoder_1_out2));  // open: Qn, preset, reset
  and and_4 (out_7, decoder_1_out0, in_5, d_ff_4_q);
  and and_5 (out_9, d_ff_5_q, in_5, decoder_1_out1);
  and and_6 (out_6, d_ff_6_q, in_5, decoder_1_out2);
endmodule
